# Fritzing sketch Untitled Sketch (saved by Fritzing 0.9.3b)
circuit board: 8.46667cm x 5.64444cm
perfboards: 1

parts:
  Part1 = Arduino Nano (Rev3.0)
  U1 = LCD-16X2 [package=lcd-16x2_noholes]
  J1 = screw terminal, 2 pins
  J2 = screw terminal, 2 pins
  R6 = Resistor [tolerance=±5% resistance=220 package=THT]
  R5 = Resistor [tolerance=±5% resistance=220 package=THT]  # not connected
  R4 = Resistor [tolerance=±5% resistance=220 package=THT]  # not connected
  J4 = screw terminal, 2 pins
  J5 = screw terminal, 2 pins
  J6 = screw terminal, 2 pins
  R7 = Resistor [tolerance=±5% resistance=220 package=THT]  # not connected
  J8 = screw terminal, 2 pins
  J9 = screw terminal, 2 pins
  J10 = Screw terminal - 2 pins [package=THT]
  J11 = Screw terminal - 2 pins [package=THT]
  J12 = Screw terminal - 2 pins [package=THT]
  J13 = Screw terminal - 2 pins [package=THT]
  J14 = Screw terminal - 2 pins [package=THT]
  R8 = Resistor [tolerance=±5% resistance=220 package=THT]  # not connected
  J15 = screw terminal, 2 pins

nets:
  N1: Part1.RESET, J9.pin2
  GND: Part1.GND, U1.VSS, J1.pin1, J8.pin2, J9.pin1
  N2: Part1.D2, U1.RS
  N3: Part1.D3, U1.E
  N4: Part1.D4, U1.DB4
  N5: Part1.D5, U1.DB5
  N6: Part1.D6, U1.DB6
  N7: Part1.D7, U1.DB7
  N8: Part1.D8, J15.pin1
  N9: Part1.D9, J2.pin1
  N10: Part1.D10, R6.Pin_1, J4.pin1
  N11: Part1.D11/MOSI, J5.pin1
  N12: Part1.D12/MISO, J6.pin1
  N13: Part1.VIN, J1.pin2
  5V: Part1.5V, U1.VDD, J10.pin1
  N14: Part1.A7, J11.pin1
  N15: Part1.A6, J11.pin2
  N16: Part1.A5, J12.pin1
  N17: Part1.A4, J12.pin2
  N18: Part1.A3, J13.pin1
  N19: Part1.A2, J13.pin2
  N20: Part1.A1, J14.pin1
  N21: Part1.A0, J14.pin2
  N22: Part1.D13/SCK, J8.pin1
  N23: U1.VO, U1.R_W
  N24: J2.pin2, J6.pin2
