# Fritzing sketch wg-brew-plus-1.0 (saved by Fritzing 0.9.3b)
circuit board: 9.85396cm x 6.14577cm
breadboards: 1

parts:
  ARDUINO-NANO = Arduino Nano (Rev3.0)
  DISPLAY_16X2 = LCD-16X2 [package=lcd-16x2_noholes]
  R-PU-A7 = Resistor [tolerance=±5% resistance=220 package=THT]
  BT2_BT3 = screw terminal, 2 pins
  BT6_BT7 = screw terminal, 2 pins
  +5V_BT1 = screw terminal, 2 pins
  +_D8_- = screw terminal, 2 pins
  +_D13_- = screw terminal, 2 pins
  A1_A0 = screw terminal, 2 pins
  A3_A2 = screw terminal, 2 pins
  A5_A4 = screw terminal, 2 pins
  A7_A6 = screw terminal, 2 pins
  -_5V_+ = screw terminal, 2 pins
  -_VIN_+ = screw terminal, 2 pins
  BT-RESET = screw terminal, 2 pins
  D-BT3 = Rectifier Diode [part_number=1N4001 package="300 mil [THT]"]
  D-BT4 = Rectifier Diode [part_number=1N4001 package="300 mil [THT]"]
  D-BT5 = Rectifier Diode [part_number=1N4001 package="300 mil [THT]"]
  D-BT6 = Rectifier Diode [part_number=1N4001 package="300 mil [THT]"]
  D-BT7 = Rectifier Diode [part_number=1N4001 package="300 mil [THT]"]
  D-BT2 = Rectifier Diode [part_number=1N4001 package="300 mil [THT]"]
  +_D9_- = screw terminal, 2 pins
  +_D8_-_2 = screw terminal, 2 pins
  R-PD-A4 = Resistor [tolerance=±5% resistance=220 package=THT]
  R-PD-A3 = Resistor [tolerance=±5% resistance=220 package=THT]
  R-PD-A0 = Resistor [tolerance=±5% resistance=220 package=THT]
  R-PU-A5 = Resistor [tolerance=±5% resistance=220 package=THT]
  R-PU-A6 = Resistor [tolerance=±5% resistance=220 package=THT]
  BUZZER = Buzzer 12mm [package=buzzer-12mm-ns-kit]
  BT4_BT5 = screw terminal, 2 pins
  R-PD-D13 = Resistor [tolerance=±5% resistance=220 package=THT]

nets:
  GND: ARDUINO-NANO.GND, DISPLAY_16X2.VSS, DISPLAY_16X2.VO, DISPLAY_16X2.R_W, DISPLAY_16X2.K, +_D8_-.pin2, +_D13_-.pin2, -_5V_+.pin2, -_VIN_+.pin2, BT-RESET.pin2, +_D9_-.pin2, +_D8_-_2.pin2, R-PD-A4.Pin_0, R-PD-A3.Pin_0, R-PD-A0.Pin_1, BUZZER.2, R-PD-D13.Pin_0
  N1: ARDUINO-NANO.D2, DISPLAY_16X2.RS
  N2: ARDUINO-NANO.D3, DISPLAY_16X2.E
  N3: ARDUINO-NANO.D4, DISPLAY_16X2.DB4
  N4: ARDUINO-NANO.D5, DISPLAY_16X2.DB5
  N5: ARDUINO-NANO.D6, DISPLAY_16X2.DB6
  N6: ARDUINO-NANO.D7, DISPLAY_16X2.DB7
  N7: ARDUINO-NANO.D8, +_D8_-.pin1
  N8: ARDUINO-NANO.D9, +_D9_-.pin1
  N9: ARDUINO-NANO.D10, +_D8_-_2.pin1
  N10: ARDUINO-NANO.D11/MOSI, BUZZER.1
  N11: ARDUINO-NANO.D12/MISO, +5V_BT1.pin1, D-BT2.cathode, R-PD-D13.Pin_1
  N12: ARDUINO-NANO.VIN, -_VIN_+.pin1
  N13: ARDUINO-NANO.RESET, BT-RESET.pin1
  5V: ARDUINO-NANO.5V, DISPLAY_16X2.VDD, DISPLAY_16X2.A, R-PU-A7.Pin_0, +5V_BT1.pin2, -_5V_+.pin1, R-PU-A5.Pin_0, R-PU-A6.Pin_0
  N14: ARDUINO-NANO.A7, R-PU-A7.Pin_1, A7_A6.pin1
  N15: ARDUINO-NANO.A6, A7_A6.pin2, R-PU-A6.Pin_1
  N16: ARDUINO-NANO.A5, A5_A4.pin1, R-PU-A5.Pin_1
  N17: ARDUINO-NANO.A4, A5_A4.pin2, R-PD-A4.Pin_1
  N18: ARDUINO-NANO.A3, A3_A2.pin1, R-PD-A3.Pin_1
  N19: ARDUINO-NANO.A2, A3_A2.pin2
  N20: ARDUINO-NANO.A1, A1_A0.pin1
  N21: ARDUINO-NANO.A0, A1_A0.pin2, R-PD-A0.Pin_0
  N22: ARDUINO-NANO.D13/SCK, +_D13_-.pin1
  N23: BT2_BT3.pin1, D-BT3.anode, D-BT4.cathode
  N24: BT2_BT3.pin2, D-BT3.cathode, D-BT2.anode
  N25: BT6_BT7.pin1, D-BT7.anode
  N26: BT6_BT7.pin2, D-BT6.anode, D-BT7.cathode
  N27: D-BT4.anode, D-BT5.cathode, BT4_BT5.pin2
  N28: D-BT5.anode, D-BT6.cathode, BT4_BT5.pin1

notes:
  WG-BREW PLUS 1.0
  WG-BREW PLUS V1.0
